# Fritzing sketch component_layout (saved by Fritzing 0.9.10b)

parts:
  Mod1 = Amica NodeMCU DEVKIT 1.0
  NEOPIXEL1 = Neopixel Strip -- White (60/m) [part_number=1138]
  Power_plug1 = Power plug
  R2 = Resistor [tolerance=±5% power=0.25 resistance=10k package=THT]
  R1 = Photocell (LDR) [package=THT]
  NEOPIXEL2 = Neopixel Strip -- White (60/m) [part_number=1138]
  R3 = Photocell (LDR) [package=THT]
  Power_plug2 = Power plug
  R4 = Resistor [tolerance=±5% power=0.25 resistance=10k package=THT]
  A1 = lolin S3 mini

nets:
  GND: Mod1.pin2, Mod1.pin_9, Mod1.pin_29, NEOPIXEL1.GND, Power_plug1.GND, R2.Pin_1
  N1: Mod1.pin4, NEOPIXEL1.DI
  N2: Mod1.pin_16, R2.Pin_0, R1.pin_1
  +5V: Mod1.pin_30, NEOPIXEL1.+5V, Power_plug1.VCC, R1.pin_0
  +5V_2: NEOPIXEL2.+5V, R3.pin_0, Power_plug2.VCC, A1.Pin_25
  N3: NEOPIXEL2.DI, A1.Pin_5
  GND_2: NEOPIXEL2.GND, Power_plug2.GND, R4.Pin_1, A1.Pin_18, A1.Pin_26
  N4: R3.pin_1, R4.Pin_0, A1.Pin_2

custom parts:
  Neopixel Strip -- White (60/m): Neopixel Strip, White, 60 pixels per meter.
  lolin S3 mini: WiFi + Bluetooth 5 (LE) boards based ESP32-S3FH4R2.
